# Fritzing sketch Esquema Deteccion de objetos (saved by Fritzing 0.8.3b)
breadboards: 1

parts:
  Parte1 = Arduino Uno (Rev3)
  Servomotor_1 = Basic Servo
  Servomotor_2 = Basic Servo

nets:
  N1: Parte1.D9_PWM, Servomotor_1.pulse
  N2: Parte1.D11_PWM/MOSI, Servomotor_2.pulse
  5V: Parte1.5V, Servomotor_2.vcc
  VIN: Parte1.VIN, Servomotor_2.gnd
